# Fritzing sketch Booze-o-meter (saved by Fritzing 0.7.12b)
perfboards: 1

parts:
  J1 = male pin header, 2 pins [form="♂ (male)"]  # not connected
  D1 = Rectifier Diode [part_number=1N4001 package="300 mil [THT]"]  # not connected
  U2 = Voltage Regulator - 5V [package="TO220 [THT]"]
  C1 = Electrolytic Capacitor [capacitance=0.1mF package="100 mil [THT, electrolytic]"]  # not connected
  C2 = Electrolytic Capacitor [capacitance=10µF package="100 mil [THT, electrolytic]"]  # not connected
  LED1 = LED - 3mm [color="Green (565nm)" package="3 mm [THT]"]  # not connected
  R1 = Resistor [tolerance=±5% resistance=220 package=THT]  # not connected
  U3 = atmega168 [package=dip]
  Y1 = Resonator [frequency="16 Mhz" package=THT]
  J3 = male pin header, 6 pins [form="♂ (male)"]
  C3 = Tantalum Capacitor [capacitance="1 μF" part_number=PTC package="100 mil [THT, tantalum]"]
  Q1 = NPN-Transistor [package="TO92 [THT]"]
  R2 = Resistor [tolerance=±5% resistance=220 package=THT]  # not connected
  J5 = male pin header, 3 pins [form="♂ (male)"]
  J6 = male pin header, 3 pins [form="♂ (male)"]
  J7 = male pin header, 3 pins [form="♂ (male)"]
  C4 = Ceramic Capacitor [capacitance=100nF package="100 mil [THT, multilayer]"]
  J8 = male pin header, 2 pins [form="♂ (male)"]
  J9 = male pin header, 4 pins [form="♂ (male)"]
  C5 = Ceramic Capacitor [capacitance=100nF package="100 mil [THT, multilayer]"]
  R3 = Resistor [tolerance=±5% resistance=220 package=THT]
  R4 = Resistor [tolerance=±5% resistance=10k package=THT]
  R5 = Resistor [tolerance=±5% resistance=1k package=THT]
  J4 = male pin header, 2 pins [form="♂ (male)"]

nets:
  N1: U2.output_voltage, C3.-
  N2: U3.D3_(PWM), J7.pin3
  N3: U3.XLAT1, Y1.pin_1
  N4: U3.D6_(PWM), J9.pin2
  N5: U3.D8, J9.pin4, R3.Pin_0
  N6: U3.D9_(PWM), J5.pin3
  N7: U3.D10_(PWM), J5.pin2
  N8: U3.D11_(PWM), J5.pin1
  N9: U3.D12, J6.pin3
  N10: U3.A1, J8.pin2
  N11: U3.A2, J6.pin2
  N12: J3.pin1, C5.1, R4.Pin_1
  N13: J3.pin6, C4.0
  N14: Q1.B, R5.Pin_0
  N15: Q1.C, J4.pin1
  N16: J7.pin1, C5.0, J4.pin2
  N17: J8.pin1, J9.pin3
  N18: J9.pin1, R4.Pin_0

notes:
  programming header
  Power In
  fan
  top 2
  top 1
  button
